// Logisim project CPU - Projeto.circ as structural Verilog: 11 circuits, main circuit CPU
module CPU (
);

  wire and_1_out, CLK, CONT_CLEAR, ENABLE_REG1, ENABLE_REG2, JUMP_CONTROL, K0, K1, K2, K3, L0, L1, L2, L3,
       L4, L5, L6, L7, L8, L9, MCLEAR, nCLK, or_1_out, or_2_out, or_3_out, REG_CLEAR, RGIN_1BIT, S1, S2, S3,
       S4, S5, S6, S7, S8;
  wire [1:0] ULA_OP;
  wire [3:0] HEX0, HEX1, HEX2, HEX3, HEX4, HEX5, multiplexer_1_out, OPERANDO, SAIDA_ULA;

  LED u_L9 (.in(L9));
  // DipSwitch #(.NSwitches(1)) S9: pin names not known; wires that end beside it: CLK
  Hex_Digit_Display hex_digit_display_1 (.value(HEX4));  // open: dp
  Hex_Digit_Display hex_digit_display_2 (.value(HEX5));  // open: dp
  LED u_L8 (.in(L8));
  LED u_L7 (.in(L7));
  // DipSwitch #(.NSwitches(1)) S8: pin names not known; wires that end beside it: S8
  // DipSwitch #(.NSwitches(1)) S6: pin names not known; wires that end beside it: S6
  // DipSwitch #(.NSwitches(1)) S7: pin names not known; wires that end beside it: S7
  Hex_Digit_Display hex_digit_display_3 (.value(HEX2));  // open: dp
  Hex_Digit_Display hex_digit_display_4 (.value(HEX3));  // open: dp
  LED u_L6 (.in(L6));
  LED u_L5 (.in(L5));
  LED u_L4 (.in(L4));
  // DipSwitch #(.NSwitches(1)) S4: pin names not known; wires that end beside it: S4
  // DipSwitch #(.NSwitches(1)) S5: pin names not known; wires that end beside it: S5
  Hex_Digit_Display hex_digit_display_5 (.value(HEX1));  // open: dp
  LED u_L1 (.in(L1));
  LED u_L2 (.in(L2));
  LED u_L3 (.in(L3));
  // DipSwitch #(.NSwitches(1)) S3: pin names not known; wires that end beside it: S3
  // DipSwitch #(.NSwitches(1)) S2: pin names not known; wires that end beside it: S2
  // DipSwitch #(.NSwitches(1)) S1: pin names not known; wires that end beside it: S1
  Hex_Digit_Display hex_digit_display_6 (.value(HEX0));  // open: dp
  LED u_L0 (.in(L0));
  // DipSwitch #(.NSwitches(1)) S0: pin names not known; wires that end beside it: MCLEAR
  Button u_K3 (.out(K3));
  Button u_K2 (.out(K2));
  Button u_K0 (.out(K0));
  Button u_K1 (.out(K1));
  UC uc_1 (
    .\Comando_hexadecimal_da_memória ({HEX5, HEX4, HEX3, HEX2}), .\Operação_de_ULA (ULA_OP),
    .Clear_registradores(REG_CLEAR), .Clear_contador(CONT_CLEAR), .Jump_Controle(JUMP_CONTROL),
    .Operando(OPERANDO), .Primeiro_Bit_do_RgIN(RGIN_1BIT), .Enable_Registrador_1(ENABLE_REG1),
    .Enable_Registrador_2(ENABLE_REG2));
  not not_1 (nCLK, CLK);
  Reg4 REG1 (.\Saída (HEX1), .in_2(CLK), .in_3(or_1_out), .\Entrada__1___Saída__0 (ENABLE_REG1), .Entrada(SAIDA_ULA));
  or or_1 (or_1_out, MCLEAR, REG_CLEAR);
  and and_1 (and_1_out, JUMP_CONTROL, CLK);
  Count8 CONT (
    .CLK(CLK), .out_5({L7, L6, L5, L4, L3, L2, L1, L0}), .CLEAR(or_2_out), .ADDRESS({4'b0000, OPERANDO}),
    .JUMP(and_1_out));
  or or_2 (or_2_out, MCLEAR, CONT_CLEAR);
  ULA4 ula4_1 (.Operacao(ULA_OP), .A(OPERANDO), .B(multiplexer_1_out), .S(SAIDA_ULA));
  Reg4 REG2 (.\Saída (HEX0), .in_2(CLK), .in_3(or_3_out), .\Entrada__1___Saída__0 (ENABLE_REG2), .Entrada(SAIDA_ULA));
  ROM_256x16 rom_256x16_1 (
    .ADDRESS({L7, L6, L5, L4, L3, L2, L1, L0}), .CLK(nCLK), .out_4({HEX5, HEX4, HEX3, HEX2}), .CLEAR(MCLEAR));
  Multiplexer #(.width(4), .enable("false")) multiplexer_1 (
    .in0(HEX0), .in1(HEX1), .out(multiplexer_1_out), .sel(RGIN_1BIT));
  or or_3 (or_3_out, MCLEAR, REG_CLEAR);

  // Other names for the same wires on the sheet: MEM_INSTRUCTION[15:0] = {HEX5, HEX4, HEX3, HEX2}; R1[3:0] = HEX1;
  //   R2[3:0] = HEX0; S0 = MCLEAR; S9 = CLK
endmodule

module UC (
  input  [15:0] \Comando_hexadecimal_da_memória ,
  output [1:0] \Operação_de_ULA ,
  output Clear_registradores,
  output Clear_contador,
  output Jump_Controle,
  output Primeiro_Bit_do_RgIN,
  output Enable_Registrador_1,
  output Enable_Registrador_2,
  output [3:0] Operando
);

  wire and_1_out, and_2_out, JMP_ULA, XOR_RgIN_CD;

  Demultiplexer #(.select(2), .enable("false")) demultiplexer_1 (
    .out0(JMP_ULA), .out1(Clear_registradores), .out2(Clear_contador), .out3(Jump_Controle), .in(1'b1),
    .sel(\Comando_hexadecimal_da_memória [11:10]));
  xor xor_1 (XOR_RgIN_CD, \Comando_hexadecimal_da_memória [14], \Comando_hexadecimal_da_memória [15]);
  and and_1 (and_1_out, ~\Comando_hexadecimal_da_memória [12], \Comando_hexadecimal_da_memória [13]);  // AND_Gate
  and and_2 (and_2_out, \Comando_hexadecimal_da_memória [12], ~\Comando_hexadecimal_da_memória [13]);  // AND_Gate
  assign \Operação_de_ULA  = \Comando_hexadecimal_da_memória [9:8] & {2{JMP_ULA}};  // AND_Gate and_3, 2 bits wide
  and and_4 (Enable_Registrador_1, and_1_out, XOR_RgIN_CD);
  and and_5 (Enable_Registrador_2, and_2_out, XOR_RgIN_CD);

  assign Operando = \Comando_hexadecimal_da_memória [3:0];
  assign Primeiro_Bit_do_RgIN = \Comando_hexadecimal_da_memória [12];

  // Other names for the same wires on the sheet: HEX_ROM[15:0] = \Comando_hexadecimal_da_memória ;
  //   DISPONIVEL[3:0] = \Comando_hexadecimal_da_memória [7:4]; ULA[1:0] = \Comando_hexadecimal_da_memória [9:8];
  //   JMP[1:0] = \Comando_hexadecimal_da_memória [11:10]; RgIN[1:0] = \Comando_hexadecimal_da_memória [13:12];
  //   RgIN_A = \Comando_hexadecimal_da_memória [12]; RgIN_B = \Comando_hexadecimal_da_memória [13];
  //   RgIN_C = \Comando_hexadecimal_da_memória [14]; RgTO[1:0] = \Comando_hexadecimal_da_memória [15:14];
  //   RgIN_D = \Comando_hexadecimal_da_memória [15]; JMP_JUMP = Jump_Controle; JMP_RESET_COUNT = Clear_contador;
  //   JMP_RESET_REG = Clear_registradores
endmodule

module Reg4 (
  input  [3:0] Entrada,
  input  in_2,
  input  in_3,
  input  \Entrada__1___Saída__0 ,
  output [3:0] \Saída 
);

  wire CLEAR, D0, D1, D2, D3;

  not not_1 (CLEAR, in_3);
  D_Flip_Flop #(.NegatePresetClear("true")) d_ff_1 (
    .clk(in_2), .D(D0), .Q(\Saída [0]), .preset(1'b1), .reset(CLEAR));  // open: Qn
  Multiplexer #(.width(4), .enable("false")) multiplexer_1 (
    .in0(\Saída ), .in1(Entrada), .out({D3, D2, D1, D0}), .sel(\Entrada__1___Saída__0 ));
  D_Flip_Flop #(.NegatePresetClear("true")) d_ff_2 (
    .clk(in_2), .D(D1), .Q(\Saída [1]), .preset(1'b1), .reset(CLEAR));  // open: Qn
  D_Flip_Flop #(.NegatePresetClear("true")) d_ff_3 (
    .clk(in_2), .D(D2), .Q(\Saída [2]), .preset(1'b1), .reset(CLEAR));  // open: Qn
  D_Flip_Flop #(.NegatePresetClear("true")) d_ff_4 (
    .clk(in_2), .D(D3), .Q(\Saída [3]), .preset(1'b1), .reset(CLEAR));  // open: Qn

  // Other names for the same wires on the sheet: CLK = in_2; I_O = \Entrada__1___Saída__0 ; Q0 = \Saída [0];
  //   SAIDA[3:0] = \Saída ; Q1 = \Saída [1]; Q2 = \Saída [2]; Q3 = \Saída [3]
endmodule

module Count8 (
  input  [7:0] ADDRESS,
  input  JUMP,
  input  CLEAR,
  input  CLK,
  output [7:0] out_5
);

  wire Q2E, Q3E, Q4E, Q5E, Q6E, Q7E;

  unidade_contador unidade_contador_1 (
    .ADDR(ADDRESS[0]), .CLK(CLK), .JUMP(JUMP), .T(1'b1), .CLEAR(CLEAR), .Q(out_5[0]));
  unidade_contador unidade_contador_2 (.ADDR(ADDRESS[4]), .CLK(CLK), .JUMP(JUMP), .T(Q4E), .CLEAR(CLEAR), .Q(out_5[4]));
  and and_1 (Q4E, Q3E, out_5[3]);
  unidade_contador unidade_contador_3 (
    .ADDR(ADDRESS[1]), .CLK(CLK), .JUMP(JUMP), .T(out_5[0]), .CLEAR(CLEAR), .Q(out_5[1]));
  unidade_contador unidade_contador_4 (.ADDR(ADDRESS[5]), .CLK(CLK), .JUMP(JUMP), .T(Q5E), .CLEAR(CLEAR), .Q(out_5[5]));
  and and_2 (Q5E, Q4E, out_5[4]);
  unidade_contador unidade_contador_5 (.ADDR(ADDRESS[2]), .CLK(CLK), .JUMP(JUMP), .T(Q2E), .CLEAR(CLEAR), .Q(out_5[2]));
  unidade_contador unidade_contador_6 (.ADDR(ADDRESS[6]), .CLK(CLK), .JUMP(JUMP), .T(Q6E), .CLEAR(CLEAR), .Q(out_5[6]));
  and and_3 (Q2E, out_5[0], out_5[1]);
  and and_4 (Q6E, Q5E, out_5[5]);
  unidade_contador unidade_contador_7 (.ADDR(ADDRESS[3]), .CLK(CLK), .JUMP(JUMP), .T(Q3E), .CLEAR(CLEAR), .Q(out_5[3]));
  unidade_contador unidade_contador_8 (.ADDR(ADDRESS[7]), .CLK(CLK), .JUMP(JUMP), .T(Q7E), .CLEAR(CLEAR), .Q(out_5[7]));
  and and_5 (Q3E, Q2E, out_5[2]);
  and and_6 (Q7E, Q6E, out_5[6]);

  // Other names for the same wires on the sheet: AD0 = ADDRESS[0]; AD1 = ADDRESS[1]; AD2 = ADDRESS[2];
  //   AD3 = ADDRESS[3]; AD4 = ADDRESS[4]; AD5 = ADDRESS[5]; AD6 = ADDRESS[6]; AD7 = ADDRESS[7]; Q0 = out_5[0];
  //   Q1E = out_5[0]; Q1 = out_5[1]; Q2 = out_5[2]; Q3 = out_5[3]; Q4 = out_5[4]; Q5 = out_5[5]; Q6 = out_5[6];
  //   Q7 = out_5[7]
endmodule

module ULA4 (
  input  [1:0] Operacao,
  input  [3:0] A,
  input  [3:0] B,
  output [3:0] S
);

  wire Sub;
  wire [3:0] D, M, S_t;

  and and_1 (Sub, ~Operacao[0], Operacao[1]);  // AND_Gate
  somador_subtrator somador_subtrator_1 (.B(B), .A(A), .Subtrair(Sub), .out_4(S_t));
  muliplicador muliplicador_1 (.A(A), .out_2(M));
  divisor divisor_1 (.A(A), .out_2(D));
  Multiplexer #(.select(2), .width(4), .enable("false")) multiplexer_1 (
    .in0(S_t), .in1(M), .in2(S_t), .in3(D), .out(S), .sel(Operacao));

  // Other names for the same wires on the sheet: Op[1:0] = Operacao
endmodule

module ROM_256x16 (
  input  [7:0] ADDRESS,
  input  CLK,
  input  CLEAR,
  output [15:0] out_4
);

  wire [7:0] register_1_q;

  Register #(.Select("low")) register_1 (.D(ADDRESS), .Q(register_1_q), .clk(CLK), .clr(CLEAR));  // open: en
  ROM #(.dataWidth(16), .Select("low")) ROM_256x16 (.addr(register_1_q), .data(out_4), .sel(1'b0));

  // Notes on the sheet:
  //   contents of ROM_256x16 (hex, n*v repeats v):
  //   6005 9101 6202 6304 c08 0 0 0 400 6001 9001 9002 6302 6102 9302 6200 6001 800
endmodule

module unidade_contador (
  input  ADDR,
  input  CLK,
  input  JUMP,
  input  T,
  input  CLEAR,
  output Q
);

  wire and_1_out, nand_1_out, nor_1_out;

  and and_1 (and_1_out, JUMP, ~ADDR);  // AND_Gate
  nand nand_1 (nand_1_out, JUMP, ~CLEAR, ADDR);  // NAND_Gate
  T_Flip_Flop #(.NegatePresetClear("true")) t_ff_1 (
    .clk(CLK), .T(T), .Q(Q), .preset(nand_1_out), .reset(nor_1_out));  // open: Qn
  nor nor_1 (nor_1_out, and_1_out, CLEAR);
endmodule

module somador_subtrator (
  input  [3:0] A,
  input  [3:0] B,
  input  Subtrair,
  output [3:0] out_4
);

  wire A0, A1, A2, A3, somador_completo_1_cout, somador_completo_2_cout, somador_completo_3_cout;

  xor xor_1 (A0, A[0], Subtrair);
  xor xor_2 (A1, A[1], Subtrair);
  xor xor_3 (A2, A[2], Subtrair);
  xor xor_4 (A3, A[3], Subtrair);
  somador_completo somador_completo_1 (.A(A0), .B(B[0]), .Cin(Subtrair), .Cout(somador_completo_1_cout), .S(out_4[0]));
  somador_completo somador_completo_2 (
    .A(A1), .B(B[1]), .Cin(somador_completo_1_cout), .Cout(somador_completo_2_cout), .S(out_4[1]));
  somador_completo somador_completo_3 (
    .A(A2), .B(B[2]), .Cin(somador_completo_2_cout), .Cout(somador_completo_3_cout), .S(out_4[2]));
  somador_completo somador_completo_4 (.A(A3), .B(B[3]), .Cin(somador_completo_3_cout), .S(out_4[3]));  // open: Cout

  // Other names for the same wires on the sheet: Sub = Subtrair
endmodule

module somador_completo (
  input  A,
  input  B,
  input  Cin,
  output S,
  output Cout
);

  wire and_1_out, and_2_out, AxorB;

  xor xor_1 (AxorB, A, B);
  and and_1 (and_1_out, AxorB, Cin);
  and and_2 (and_2_out, A, B);
  xor xor_2 (S, Cin, AxorB);
  or or_1 (Cout, and_1_out, and_2_out);
endmodule

module muliplicador (
  input  [3:0] A,
  output [3:0] out_2
);


  assign out_2 = {A[2:0], 1'b0};
endmodule

module divisor (
  input  [3:0] A,
  output [3:0] out_2
);


  assign out_2 = {1'b0, A[3:1]};
endmodule
