// Logisim project elevador_projeto_final.circ as structural Verilog: 1 circuit, main circuit main
module main (
  input  S9,
  input  S8,
  input  S7,
  input  S6,
  input  S5,
  input  S4,
  input  S3,
  input  S2,
  input  S1,
  input  S0
);

  wire K0, K1, K2, K3, L6, L7;
  wire [3:0] ANDAR_ATUAL, HEX1, HEX2, HEX3, HEX4;

  Hex_Digit_Display hex_digit_display_1 (.value({S4, S3, S2, S1}));  // open: dp
  Hex_Digit_Display hex_digit_display_2 (.value(HEX4));  // open: dp
  LED L8 (.in(S8));
  LED u_L7 (.in(L7));
  LED L9 (.in(S9));
  Hex_Digit_Display hex_digit_display_3 (.value(HEX3));  // open: dp
  LED L4 (.in(S4));
  LED u_L6 (.in(L6));
  LED L5 (.in(S5));
  Hex_Digit_Display hex_digit_display_4 (.value(HEX1));  // open: dp
  Hex_Digit_Display hex_digit_display_5 (.value(HEX2));  // open: dp
  LED L2 (.in(S2));
  LED L3 (.in(S3));
  Hex_Digit_Display hex_digit_display_6 (.value(ANDAR_ATUAL));  // open: dp
  LED L0 (.in(S0));
  LED L1 (.in(S1));
  Button u_K3 (.out(K3));
  Button u_K2 (.out(K2));
  // VHDL_Entity #(.content("library ieee;\nuse ieee.std_logic_1164.all;\nuse ieee.numeric_std.all;\n\nentity elevador is \n	port(\n			clk: in std_logic;\n			reset: in std_logic;\n			andar_digitado: in std_logic_vector (3 downto 0);\n			andar_atual: out std_logic_vector (3 downto 0);\n			saida: out std_logic_vector (1 downto 0)			\n	);\n			\nend elevador;\n\narchitecture arch of elevador is\n	\n	signal sig_estado: std_logic_vector (1 downto 0);\n	signal sig_andar_atual: integer range 0 to 15;\n	signal sig_andar_destino: integer range 0 to 15;\n	signal sig_saida: std_logic_vector (1 downto 0);\n	\nbegin\n\n	process(clk, reset)\n	\n		variable var_entrada: std_logic_vector (1 downto 0);\n		variable var_saida: std_logic_vector (1 downto 0);\n		\n	begin\n	\n		if (reset = '1') then\n			\n			sig_estado <= \"00\";\n			sig_andar_atual <= 0;\n			sig_andar_destino <= 0;\n			sig_saida <= \"00\";\n		\n		elsif (clk'event and '0' = clk) then\n			\n			-- TRATAR ENTRADA\n			\n			if (sig_andar_destino = sig_andar_atual) then\n				var_entrada := \"00\"; -- chegou no andar\n				\n			elsif (to_integer(unsigned(andar_digitado)) < sig_andar_atual) then\n				var_entrada := \"01\"; -- pediu para descer\n				\n			elsif (to_integer(unsigned(andar_digitado)) > sig_andar_atual) then\n				var_entrada := \"10\"; -- pediu para subir\n				\n			end if;\n		\n			-- FIM TRATAR ENTRADA\n		\n			-- MAQUINA DE ESTADOS\n			\n			case sig_estado is\n			\n				when \"00\" => -- Estado Parado\n					\n					case var_entrada is\n						\n						when \"00\" => -- Chegou no andar\n							sig_estado <= \"00\";\n							var_saida := \"00\";\n					\n						when \"01\" => -- Pediu para descer\n							sig_estado <= \"01\";\n							var_saida := \"01\";\n						\n						when \"10\" => -- Pediu para subir\n							sig_estado <= \"10\";\n							var_saida := \"10\";\n						\n						when others =>\n						\n					end case;\n				\n				when \"01\" => -- Estado Descendo\n					\n					case var_entrada is\n						\n						when \"00\" => -- Chegou no andar\n							sig_estado <= \"00\";\n							var_saida := \"00\";\n					\n						when \"01\" => -- Pediu para descer\n							sig_estado <= \"01\";\n							var_saida := \"01\";\n						\n						when \"10\" => -- Pediu para subir\n							sig_estado <= \"01\";\n							var_saida := \"01\";\n						\n						when others =>\n						\n					end case;\n				\n				when \"10\" => -- Estado Subindo\n					\n					case var_entrada is\n						\n						when \"00\" => -- Chegou no andar\n							sig_estado <= \"00\";\n							var_saida := \"00\";\n					\n						when \"01\" => -- Pediu para descer\n							sig_estado <= \"10\";\n							var_saida := \"10\";\n						\n						when \"10\" => -- Pediu para subir\n							sig_estado <= \"10\";\n							var_saida := \"10\";\n						\n						when others =>\n						\n					end case;\n				\n				when others =>\n			\n			end case;\n			\n			sig_saida <= var_saida;\n			\n			-- FIM MAQUINA DE ESTADOS		\n		\n		elsif (clk'event and '1' = clk) then\n		\n			-- TRATAR SAIDA\n			\n			if (sig_saida = \"00\") then -- Parar\n				sig_andar_destino <= to_integer(unsigned(andar_digitado));\n			\n			elsif (sig_saida= \"01\") then -- Descer\n				sig_andar_atual <= sig_andar_atual - 1;\n			\n			elsif (sig_saida = \"10\") then -- Subir\n				sig_andar_atual <= sig_andar_atual + 1;\n			\n			end if;\n			\n			-- FIM TRATAR SAIDA	\n		\n		end if;\n	\n	end process;\n	\n	-- Saidas assincronas\n	andar_atual <= std_logic_vector(to_unsigned(sig_andar_atual, andar_atual'length));	\n	saida <= sig_saida;\n	\nend arch;")) vhdl_entity_1: pin names not known; wires that end beside it: S9, S0, {S4, S3, S2, S1}, ANDAR_ATUAL, {L7, L6}
  Button u_K1 (.out(K1));
  Button u_K0 (.out(K0));

  // Other names for the same wires on the sheet: HEX0[3:0] = ANDAR_ATUAL; ANDAR_DIGITADO[3:0] = {S4, S3, S2, S1};
  //   HEX5[3:0] = {S4, S3, S2, S1}; SAIDA[1:0] = {L7, L6}
endmodule
