// Logisim project refrigerante_projeto_final.circ as structural Verilog: 1 circuit, main circuit main
module main (
  input  S9,
  input  S8,
  input  S7,
  input  S6,
  input  S5,
  input  S4,
  input  S3,
  input  S2,
  input  S1,
  input  S0
);

  wire K0, K1, K2, K3, L6, L7;
  wire [3:0] divider_4_out, HEX0, HEX1, HEX2, HEX3, HEX4, HEX5;
  wire [7:0] divider_2_rem, vhdl_entity_1_p9;
  wire [7:4] divider_1_rem, divider_3_out;

  Hex_Digit_Display hex_digit_display_1 (.value(HEX4));  // open: dp
  Hex_Digit_Display hex_digit_display_2 (.value(HEX5));  // open: dp
  LED L9 (.in(S9));
  LED L8 (.in(S8));
  LED u_L7 (.in(L7));
  Hex_Digit_Display hex_digit_display_3 (.value(HEX3));  // open: dp
  LED L5 (.in(S5));
  LED L4 (.in(S4));
  LED u_L6 (.in(L6));
  Hex_Digit_Display hex_digit_display_4 (.value(HEX1));  // open: dp
  Hex_Digit_Display hex_digit_display_5 (.value(HEX2));  // open: dp
  LED L3 (.in(S3));
  LED L2 (.in(S2));
  Hex_Digit_Display hex_digit_display_6 (.value(HEX0));  // open: dp
  LED L0 (.in(S0));
  LED L1 (.in(S1));
  Button u_K3 (.out(K3));
  Button u_K2 (.out(K2));
  Button u_K0 (.out(K0));
  Button u_K1 (.out(K1));
  // VHDL_Entity #(.content("library ieee;\nuse ieee.std_logic_1164.all;\nuse ieee.numeric_std.all;\n\nentity refrigerante is \n	port(\n			clk: in std_logic;\n			reset: in std_logic;\n			entrada_10: in std_logic;\n			entrada_25: in std_logic;\n			entrada_50: in std_logic;\n			entrada_100: in std_logic;\n			botao: in std_logic;\n			saida: out std_logic_vector (1 downto 0);\n			dinheiro: out std_logic_vector (7 downto 0)\n	);\n			\nend refrigerante;\n\narchitecture arch of refrigerante is\n	\n	signal sig_estado: std_logic_vector (1 downto 0);\n	signal sig_saida: std_logic_vector (1 downto 0);\n	signal sig_dinheiro: integer range 0 to 255;\n	signal sig_dinheiro_aux: integer range 0 to 255;\n	\nbegin\n\n	process(clk, reset)\n	\n		variable var_entrada: std_logic_vector (1 downto 0);\n		variable var_saida: std_logic_vector (1 downto 0);\n		variable var_dinheiro: integer range 0 to 255;\n		\n	begin\n	\n		if (reset = '1') then\n			\n			sig_estado <= \"00\";\n			sig_saida <= \"00\";\n			sig_dinheiro <= 0;\n			var_dinheiro := 0;\n		\n		elsif (clk'event and '1' = clk) then\n			\n			-- TRATAR ENTRADA\n			\n			var_dinheiro := sig_dinheiro;\n			\n			-- Entrada de dinheiro\n			\n			if (entrada_100 = '1') then\n				var_dinheiro := var_dinheiro + 100;\n			\n			elsif (entrada_50 = '1') then\n				var_dinheiro := var_dinheiro + 50;\n			\n			elsif (entrada_25 = '1') then\n				var_dinheiro := var_dinheiro + 25;\n			\n			elsif (entrada_10 = '1') then\n				var_dinheiro := var_dinheiro + 10;\n			\n			end if;\n			\n			-- Fim entrada de dinheiro\n			\n			\n			-- Definir entrada da MEF			\n			\n			if (botao = '1') then\n				var_entrada := \"00\"; -- botão apertado\n			\n			elsif (var_dinheiro = 100) then\n				var_entrada := \"11\"; -- dinheiro correto\n				\n			elsif (var_dinheiro < 100 and var_dinheiro > 0) then\n				var_entrada := \"01\"; -- dinheiro abaixo\n				\n			elsif (var_dinheiro > 100) then\n				var_entrada := \"10\"; -- dinheiro acima\n			\n			else\n				var_entrada := \"00\"; -- dinheiro = 0\n			\n			end if;\n			\n			-- Fim definir entrada da MEF\n		\n			-- FIM TRATAR ENTRADA\n			\n		\n			-- MÁQUINA DE ESTADOS\n			\n			case sig_estado is\n			\n				when \"00\" => -- Esperando Dinheiro\n					\n					case var_entrada is\n						\n						when \"00\" => -- Botão\n							sig_estado <= \"00\"; -- ED\n							var_saida := \"00\";  -- Nada\n					\n						when \"01\" => -- Abaixo\n							sig_estado <= \"01\"; -- GD\n							var_saida := \"00\";  -- Nada\n						\n						when \"10\" => -- Acima\n							sig_estado <= \"00\"; -- ED\n							var_saida := \"01\";  -- Devolve\n							\n						\n						when \"11\" => -- Correto\n							sig_estado <= \"10\"; -- DC\n							var_saida := \"00\";  -- Nada\n							\n						\n						when others =>\n						\n					end case;\n				\n				when \"01\" => -- Guardando Dinheiro\n					\n					case var_entrada is\n						\n						when \"00\" => -- Botão\n							sig_estado <= \"00\"; -- ED\n							var_saida := \"01\";  -- Devolve\n					\n						when \"01\" => -- Abaixo\n							sig_estado <= \"01\"; -- GD\n							var_saida := \"00\";  -- Nada\n						\n						when \"10\" => -- Acima\n							sig_estado <= \"00\"; -- ED\n							var_saida := \"01\";  -- Devolve\n						\n						when \"11\" => -- Correto\n							sig_estado <= \"10\"; -- DC\n							var_saida := \"00\";  -- Nada\n\n						\n						when others =>\n						\n					end case;\n				\n				when \"10\" => -- Dinheiro Correto\n					\n					case var_entrada is\n						\n						when \"00\" => -- Botão\n							sig_estado <= \"00\"; -- ED\n							var_saida := \"10\";  -- Libera\n					\n						when \"01\" => -- Abaixo\n							sig_estado <= \"01\"; -- GD\n							var_saida := \"00\";  -- Nada\n						\n						when \"10\" => -- Acima\n							sig_estado <= \"00\"; -- ED\n							var_saida := \"01\";  -- Devolve\n						\n						when \"11\" => -- Correto\n							sig_estado <= \"10\"; -- DC\n							var_saida := \"00\";  -- Nada\n						\n						when others =>\n						\n					end case;\n				\n				when others =>\n			\n			end case;\n			\n			sig_saida <= var_saida;\n			sig_dinheiro_aux <= var_dinheiro;\n			\n			-- FIM MÁQUINA DE ESTADOS\n		\n		elsif (clk'event and '0' = clk) then\n			\n			-- TRATAR SAÍDA\n			\n			if (sig_saida = \"00\") then -- Nada\n				sig_dinheiro <= sig_dinheiro_aux;\n			\n			elsif (sig_saida= \"01\") then -- Devolver\n				sig_dinheiro <= 0;\n			\n			elsif (sig_saida = \"10\") then -- Liberar\n				sig_dinheiro <= 0;\n			\n			end if;\n			\n			-- FIM TRATAR SAÍDA	\n		\n		end if;\n	\n	end process;\n	\n	-- Saídas assíncronas\n	dinheiro <= std_logic_vector(to_unsigned(sig_dinheiro, dinheiro'length));	\n	saida <= sig_saida;\n	\nend arch;")) vhdl_entity_1: pin names not known; wires that end beside it: S9, S0, S1, S2, S3, S4, S8, {L7, L6}, vhdl_entity_1_p9
  Divider divider_1 (.a(vhdl_entity_1_p9), .b(8'ha), .rem({divider_1_rem, HEX0}));  // open: out, upper
  Divider divider_2 (.a(vhdl_entity_1_p9), .b(8'h64), .rem(divider_2_rem));  // open: out, upper
  Divider divider_3 (.a(vhdl_entity_1_p9), .b(8'h64), .out({divider_3_out, HEX2}));  // open: upper, rem
  Divider divider_4 (.a(divider_2_rem), .b(8'ha), .out({divider_4_out, HEX1}));  // open: upper, rem

  // Other names for the same wires on the sheet: SAIDA[1:0] = {L7, L6}
endmodule
